# Fritzing sketch motorcontrol (saved by Fritzing 0.8.7b)

parts:
  RaspberryPi1 = Raspberry Pi Model B
  Part1 = EasyDriver_v44
  R1 = Resistor [tolerance=±5% resistance=1k package=THT]
  R2 = Resistor [tolerance=±5% resistance=1k package=THT]
  M1 = Stepper Motor - Bipolar

nets:
  N1: RaspberryPi1.#23, Part1.STEP, R1.Pin_1
  N2: RaspberryPi1.#24, Part1.DIR, R2.Pin_1
  N3: Part1.GND, Part1.MS2
  N4: Part1.OUT2A, M1.A
  N5: Part1.OUT2B, M1.C
  N6: Part1.OUT1A, M1.B
  N7: Part1.OUT1B, M1.D

notes:
  12 Volts

custom parts:
  Raspberry Pi Model B: Raspberry Pi (Model B)
