# Fritzing sketch motorcontrolandrfids_schem (saved by Fritzing 0.8.7b)

parts:
  M1 = Stepper Motor - Bipolar
  Part1 = EasyDriver_v44
  RFID1 = RFID Reader  # not connected
  RaspberryPi1 = Raspberry Pi Model B
  R1 = Resistor [tolerance=±5% resistance=1k package=THT]
  R2 = Resistor [tolerance=±5% resistance=1k package=THT]

nets:
  N1: M1.A, Part1.OUT2A
  N2: M1.C, Part1.OUT2B
  N3: M1.B, Part1.OUT1A
  N4: M1.D, Part1.OUT1B
  GND: Part1.GND, Part1.MS1, Part1.MS2, RaspberryPi1.GND, R1.Pin_0, R2.Pin_0
  N5: Part1.STEP, RaspberryPi1.#23, R2.Pin_1
  N6: Part1.DIR, RaspberryPi1.#24, R1.Pin_1
  N7: Part1.ENABLE, RaspberryPi1.#25

custom parts:
  Raspberry Pi Model B: Raspberry Pi (Model B)
